# Fritzing sketch ScienceFairWiring (saved by Fritzing 0.9.2b)
breadboards: 1

parts:
  Part1 = Arduino Uno (Rev3)
  LED2 = LED - 5mm [color="Red (633nm)" package="5 mm [THT]"]
  LED3 = LED - 5mm [color="Red (633nm)" package="5 mm [THT]"]
  LED4 = LED - 5mm [color="Red (633nm)" package="5 mm [THT]"]
  R1 = Resistor [tolerance=±5% resistance=220 package=THT]
  LED1 = LED - 5mm [color="Red (633nm)" package="5 mm [THT]"]
  R2 = Resistor [tolerance=±5% resistance=220 package=THT]

nets:
  N1: Part1.D8, LED1.anode
  N2: Part1.D13/SCK, LED3.anode
  N3: Part1.GND, R1.Pin_1, R2.Pin_0
  N4: Part1.D2, R2.Pin_1
  N5: Part1.D4, LED2.anode
  N6: Part1.3V3, LED4.anode
  N7: LED2.cathode, LED3.cathode, LED4.cathode, R1.Pin_0, LED1.cathode

notes:
  To Terminal 1
  To Terminal 2
  To GND Terminal
